// Logisim project LC-2200-16.circ as structural Verilog: 2 circuits, main circuit main
module main (
  output [15:0] out_1,
  output [24:0] out_2
);

  wire CLK, comparator_1_eq, Z_q;
  wire [0:0] IR_q;
  wire [1:0] Zbit;
  wire [2:0] OPCode;
  wire [3:0] RegNo, RX, RY, RZ;
  wire [5:0] multiplexer_1_out, rom_1_data, rom_2_data, State_Reg_q;
  wire [15:0] A_q, ALU_output, B_q, bit_extender_2_out, MAR_q, PC_q, ram_1_data, ram_2_data;

  Register #(.width(16)) PC (.D(out_1), .en(out_2[11]), .Q(PC_q), .clk(CLK));  // open: clr
  Clock clock_1 (.out(CLK));
  Register #(.width(16)) A (.D(out_1), .en(out_2[14]), .Q(A_q), .clk(CLK));  // open: clr
  assign out_1 = out_2[9] ? PC_q : 16'bz;  // Controlled_Buffer controlled_buffer_1
  Register #(.width(16)) B (.D(out_1), .en(out_2[15]), .Q(B_q), .clk(CLK));  // open: clr
  ALU ALU (.Output(ALU_output), .A(A_q), .B(B_q), .func(out_2[22:21]));
  assign out_1 = out_2[8] ? ALU_output : 16'bz;  // Controlled_Buffer controlled_buffer_2
  Register #(.width(16)) MAR (.D(out_1), .en(out_2[13]), .Q(MAR_q), .clk(CLK));  // open: clr
  Register #(.width(1)) Z (.D(comparator_1_eq), .en(out_2[16]), .Q(Z_q), .clk(CLK));  // open: clr
  Comparator #(.width(16)) comparator_1 (.a(out_1), .b({16{1'b0}}), .eq(comparator_1_eq));  // open: gt, lt
  assign Zbit = {{1{Z_q}}, Z_q};  // Bit_Extender bit_extender_1
  RAM #(.addrWidth(4), .dataWidth(16), .bus("separate")) ram_1 (
    .addr(RegNo), .din(out_1), .data(ram_1_data), .str(out_2[17]), .clk(CLK), .ld(1'b1));  // open: sel, clr
  assign out_1 = out_2[6] ? ram_1_data : 16'bz;  // Controlled_Buffer controlled_buffer_3
  ROM #(.addrWidth(3), .dataWidth(6)) rom_1 (.addr(OPCode), .data(rom_1_data));  // open: sel
  ROM #(.addrWidth(2), .dataWidth(6)) rom_2 (.addr(Zbit), .data(rom_2_data));  // open: sel
  Multiplexer #(.select(2), .width(6), .enable("false")) multiplexer_1 (
    .in0(out_2[5:0]), .in1(rom_1_data), .in2(rom_2_data), .out(multiplexer_1_out), .sel(out_2[24:23]));  // open: in3
  Register #(.width(6)) State_Reg (.D(multiplexer_1_out), .Q(State_Reg_q), .clk(CLK));  // open: en, clr
  RAM #(.addrWidth(16), .dataWidth(16), .bus("separate")) ram_2 (
    .addr(MAR_q), .din(out_1), .data(ram_2_data), .str(out_2[18]), .clk(CLK), .ld(1'b1));  // open: sel, clr
  assign out_1 = out_2[7] ? ram_2_data : 16'bz;  // Controlled_Buffer controlled_buffer_4
  ROM #(.addrWidth(6), .dataWidth(25)) rom_3 (.addr(State_Reg_q), .data(out_2));  // open: sel
  Register #(.width(16)) IR (.D(out_1), .en(out_2[12]), .Q({OPCode, RX, RY, RZ, IR_q[0]}), .clk(CLK));  // open: clr
  assign bit_extender_2_out = {{11{RZ[3]}}, {RZ, IR_q[0]}};  // Bit_Extender bit_extender_2
  assign out_1 = out_2[10] ? bit_extender_2_out : 16'bz;  // Controlled_Buffer controlled_buffer_5
  Multiplexer #(.select(2), .width(4), .enable("false")) multiplexer_2 (
    .in0(RX), .in1(RY), .in2(RZ), .out(RegNo), .sel(out_2[20:19]));  // open: in3

  // Other names for the same wires on the sheet: RegSelLo = out_2[19]; RegSelHi = out_2[20]; ALULo = out_2[21];
  //   func[1:0] = out_2[22:21]; ALUHi = out_2[22]; DrREG = out_2[6]; DrMEM = out_2[7]; DrALU = out_2[8];
  //   DrPC = out_2[9]; DrOFF = out_2[10]; LdPC = out_2[11]; LdIR = out_2[12]; LdMAR = out_2[13]; LdA = out_2[14];
  //   LdB = out_2[15]; LdZ = out_2[16]; WrREG = out_2[17]; WrMEM = out_2[18]
endmodule

module ALU (
  input  [15:0] A,
  input  [15:0] B,
  input  [1:0] func,
  output [15:0] Output
);

  wire [15:0] ADD, INC, NAND, nand_1_out, SUB;

  assign nand_1_out = ~(B & B);  // NAND_Gate nand_1, 16 bits wide
  Adder #(.width(16)) adder_1 (.a(A), .b(B), .out(ADD), .cin(1'b0));  // open: cout
  assign NAND = ~(A & B);  // NAND_Gate nand_2, 16 bits wide
  Adder #(.width(16)) adder_2 (.a(A), .b(nand_1_out), .out(SUB), .cin(1'b1));  // open: cout
  Adder #(.width(16)) adder_3 (.a(A), .b({16{1'b0}}), .out(INC), .cin(1'b1));  // open: cout
  Multiplexer #(.select(2), .width(16)) multiplexer_1 (
    .in0(ADD), .in1(NAND), .in2(SUB), .in3(INC), .out(Output), .sel(func));  // open: en
endmodule
